# Fritzing sketch caixa (saved by Fritzing 0.9.3b)
breadboards: 1

parts:
  Arduino1 = Arduino Uno (Rev3)
  J1 = Piezo Speaker
  R3 = Photocell (LDR) [package=THT]
  R4 = Resistor [tolerance=±5% resistance=220 package="1206 [SMD]"]
  LED1 = smd LED [color="Yellow (592nm)" package="0805 [SMD]"]
  LED2 = smd LED [color="Yellow (592nm)" package="0805 [SMD]"]
  LED3 = smd LED [color="Yellow (592nm)" package="0805 [SMD]"]
  LED4 = smd LED [color="Yellow (592nm)" package="0805 [SMD]"]

nets:
  N1: Arduino1.A0, R3.pin_0, R4.Pin_1
  N2: Arduino1.D10_PWM/SS, J1.pin1, LED1.cathode, LED2.cathode, LED3.cathode, LED4.cathode
  N3: Arduino1.5V, R3.pin_1
  N4: Arduino1.GND, J1.pin2, R4.Pin_0, LED1.anode, LED2.anode, LED3.anode, LED4.anode

notes:
  BLINK
  caixa interativa de led + piezo + LDR

// code stored in the sketch: Blink.ino
/*
  Blink
  
  Switching a LED on and off
  
  This example is part of the Fritzing Creator Kit: www.fritzing.org/creator-kit.
*/

int led = 13;                   // integer variable led is declared

void setup() {                  // the setup() method is executed only once
  pinMode(led, OUTPUT);         // the led PIN is declared as digital output
}

void loop() {                   // the loop() method is repeated
  digitalWrite(led, HIGH);      // switching on the led 
  delay(1000);                  // stopping the program for 1000 milliseconds
  digitalWrite(led, LOW);       // switching off the led 
  delay(1000);                  // stopping the program for 1000 milliseconds
}
