# Fritzing sketch exemplo esquemático (saved by Fritzing 0.9.3b)
breadboards: 1

parts:
  Arduino1 = Arduino Uno (Rev3)
  R1 = Photocell (LDR) [package=THT]
  R2 = Resistor [tolerance=±5% resistance=220 package="1206 [SMD]"]
  R3 = Photocell (LDR) [package=THT]
  R4 = Resistor [tolerance=±5% resistance=220 package="1206 [SMD]"]
  R5 = Photocell (LDR) [package=THT]
  R6 = Resistor [tolerance=±5% resistance=220 package="1206 [SMD]"]

nets:
  N1: Arduino1.A0, R1.pin_0, R2.Pin_1
  N2: Arduino1.A1, R3.pin_0, R4.Pin_1
  N3: Arduino1.A2, R5.pin_0, R6.Pin_1
  N4: Arduino1.5V, R1.pin_1, R3.pin_1, R5.pin_1
  N5: Arduino1.GND, R2.Pin_0, R4.Pin_0, R6.Pin_0

notes:
  BLINK
  conectados ao topo de uma pirâmide de papel machê

// code stored in the sketch: Blink.ino
/*
  Blink
  
  Switching a LED on and off
  
  This example is part of the Fritzing Creator Kit: www.fritzing.org/creator-kit.
*/

int led = 13;                   // integer variable led is declared

void setup() {                  // the setup() method is executed only once
  pinMode(led, OUTPUT);         // the led PIN is declared as digital output
}

void loop() {                   // the loop() method is repeated
  digitalWrite(led, HIGH);      // switching on the led 
  delay(1000);                  // stopping the program for 1000 milliseconds
  digitalWrite(led, LOW);       // switching off the led 
  delay(1000);                  // stopping the program for 1000 milliseconds
}
